// Logisim project cpu.circ as structural Verilog: 15 circuits, main circuit main
// PC
module main (
);

  wire Clk, IRWrite, IsZero, MemAddSrc, MemRead, MemWrite, PCSrc, PCWrite, RegSrc, RegWrite, Reset,
       SPControl, SPWrite;
  wire [1:0] ALUSrc, MemToReg;
  wire [2:0] ALUControl;
  wire [3:0] Read_Reg2, Write_Reg;
  wire [11:0] adder_1_out, multiplexer_1_out, multiplexer_7_out, PC_Plus_1, PC_q, RAM_Address, SP_q,
       subtractor_1_out;
  wire [17:0] ALU_Result, bit_extender_4_out, bit_extender_5_out, Imm5_Ext, Imm9_Ext, IR_Bus, Jump_Offset,
       multiplexer_5_out, RAM_Data_Out, Read_Data1, Read_Data2, rom_1_data, Write_Data;

  Clock Clock (.out(Clk));
  Button u_Reset (.out(Reset));
  Multiplexer #(.width(12), .enable("false")) multiplexer_1 (
    .in0(PC_Plus_1), .in1(IR_Bus[11:0]), .out(multiplexer_1_out), .sel(PCSrc));
  Register #(.width(12)) PC (.D(multiplexer_1_out), .en(PCWrite), .Q(PC_q), .clk(Clk), .clr(Reset));
  Multiplexer #(.width(4), .enable("false")) multiplexer_2 (
    .in0(IR_Bus[12:9]), .in1(4'b1111), .out(Write_Reg), .sel(RegSrc));
  Multiplexer #(.width(4), .enable("false")) multiplexer_3 (
    .in0(IR_Bus[4:1]), .in1(IR_Bus[12:9]), .out(Read_Reg2), .sel(MemWrite));
  ROM #(.addrWidth(12), .dataWidth(18)) rom_1 (.addr(PC_q), .data(rom_1_data));  // open: sel
  _12bitADDER u_12bitadder_1 (.A(PC_q), .B(12'h1), .Q(PC_Plus_1));  // open: CO
  Register #(.width(18)) IR (.D(rom_1_data), .en(IRWrite), .Q(IR_Bus), .clk(Clk), .clr(Reset));
  assign Imm5_Ext = {{13{IR_Bus[4]}}, IR_Bus[4:0]};  // Bit_Extender bit_extender_1
  assign Imm9_Ext = {{9{IR_Bus[8]}}, IR_Bus[8:0]};  // Bit_Extender bit_extender_2
  assign Jump_Offset = {{5{IR_Bus[12]}}, IR_Bus[12:0]};  // Bit_Extender bit_extender_3
  ControlUnit controlunit_1 (
    .IsZero(IsZero), .Opcode(IR_Bus[17:13]), .Clk(Clk), .Reset(Reset), .MemWrite(MemWrite),
    .MemRead(MemRead), .RegSrc(RegSrc), .IRWrite(IRWrite), .PCWrite(PCWrite), .MemAddSrc(MemAddSrc),
    .RegWrite(RegWrite), .PCSrc(PCSrc), .SPWrite(SPWrite), .SPControl(SPControl), .ALUSrc(ALUSrc),
    .MemToReg(MemToReg), .ALUControl(ALUControl));
  assign bit_extender_4_out = {{6{PC_Plus_1[11]}}, PC_Plus_1};  // Bit_Extender bit_extender_4
  RegisterFile registerfile_1 (
    .Write_Data(Write_Data), .RegWrite(RegWrite), .WriteReg(Write_Reg), .Clk(Clk), .ReadData1(Read_Data1),
    .ReadReg1(IR_Bus[8:5]), .ReadData2(Read_Data2), .ReadReg2(Read_Reg2));
  Multiplexer #(.select(2), .width(18), .enable("false")) multiplexer_4 (
    .in0(ALU_Result), .in1(RAM_Data_Out), .in2(bit_extender_4_out), .out(Write_Data), .sel(MemToReg));  // open: in3
  assign bit_extender_5_out = {{13{1'b0}}, IR_Bus[4:0]};  // Bit_Extender bit_extender_5
  Multiplexer #(.select(2), .width(18), .enable("false")) multiplexer_5 (
    .in0(Read_Data2), .in1(Imm5_Ext), .in2(bit_extender_5_out), .in3(Imm9_Ext), .out(multiplexer_5_out),
    .sel(ALUSrc));
  Register #(.width(12)) SP (.D(multiplexer_7_out), .en(SPWrite), .Q(SP_q), .clk(Clk), .clr(Reset));
  ALU alu_1 (.A(Read_Data1), .B(multiplexer_5_out), .ALUOp(ALUControl), .Zero_Flag(IsZero), .Result(ALU_Result));
  Adder #(.width(12)) adder_1 (.a(12'h1), .b(SP_q), .out(adder_1_out));  // open: cin, cout
  Subtractor #(.width(12)) subtractor_1 (.a(SP_q), .b(12'h1), .out(subtractor_1_out));  // open: bin, bout
  Multiplexer #(.width(12), .enable("false")) multiplexer_6 (
    .in0(ALU_Result[11:0]), .in1(SP_q), .out(RAM_Address), .sel(MemAddSrc));
  RAM #(.addrWidth(12), .dataWidth(18), .bus("separate")) ram_1 (
    .addr(RAM_Address), .din(Read_Data2), .data(RAM_Data_Out), .str(MemWrite), .sel(1'b1), .clk(Clk),
    .ld(1'b1), .clr(Reset));
  Multiplexer #(.width(12), .enable("false")) multiplexer_7 (
    .in0(adder_1_out), .in1(subtractor_1_out), .out(multiplexer_7_out), .sel(SPControl));

  // Other names for the same wires on the sheet: Read_Reg1[3:0] = IR_Bus[8:5]; OpCode[4:0] = IR_Bus[17:13]

  // Notes on the sheet:
  //   contents of rom_1 (hex, n*v repeats v):
  //   16004 c20f c20f c20f c40a 14005
endmodule

module ControlUnit (
  input  IsZero,
  input  [4:0] Opcode,
  input  Clk,
  input  Reset,
  output MemWrite,
  output MemRead,
  output RegSrc,
  output IRWrite,
  output PCWrite,
  output MemAddSrc,
  output RegWrite,
  output PCSrc,
  output SPWrite,
  output SPControl,
  output [1:0] ALUSrc,
  output [1:0] MemToReg,
  output [2:0] ALUControl
);

  wire ADD, ADDI, and_1_out, and_4_out, and_5_out, and_6_out, and_7_out, CMOV, JUMP, LD, LUI, NAND, NANDI,
       NOR, NORI, not_1_out, or_1_out, or_2_out, or_3_out, or_4_out, or_7_out, or_16_out, or_17_out, POP,
       SRA, SRL, ST, SUB, SUBI, T1_Execute, T2_Mem_Access, T3_Write_Back;
  wire [2:0] Current_State, Next_State, State1, State2;

  Decoder #(.select(5), .enable("false")) decoder_1 (
    .out0(ADD), .out1(SUB), .out2(NAND), .out3(NOR), .out4(SRL), .out5(SRA), .out6(ADDI), .out7(SUBI),
    .out8(NANDI), .out9(NORI), .out10(JUMP), .out11(MemToReg[1]), .out12(LD), .out13(ST), .out14(LUI),
    .out15(CMOV), .out16(SPControl), .out17(POP), .sel(Opcode));  // open: out18, out19, out20, out21, out22, out23, out24, out25, out26, out27, out28, out29, out30, out31
  or or_1 (or_1_out, ST, SPControl);
  or or_2 (or_2_out, LD, POP);
  or or_3 (or_3_out, JUMP, MemToReg[1]);
  and and_1 (and_1_out, or_3_out, T1_Execute);
  or or_4 (or_4_out, ST, SPControl, JUMP, LD, POP, CMOV);
  not not_1 (not_1_out, or_4_out);
  and and_2 (MemWrite, or_1_out, T2_Mem_Access);
  and and_3 (MemRead, or_2_out, T2_Mem_Access);
  or or_5 (PCWrite, and_1_out, IRWrite);
  or or_6 (MemAddSrc, SPControl, POP);
  and and_4 (and_4_out, not_1_out, T1_Execute);
  and and_5 (and_5_out, CMOV, T1_Execute, IsZero);
  or or_7 (or_7_out, JUMP, MemToReg[1]);
  and and_6 (and_6_out, SPControl, T1_Execute);
  and and_7 (and_7_out, POP, T3_Write_Back);
  or or_8 (ALUSrc[0], SPControl, ADDI, SUBI, NANDI, NORI, LUI, LD, ST, POP);
  or or_9 (ALUSrc[1], ST, SRL, SRA, NANDI, NORI, LD);
  or or_10 (MemToReg[0], LD, POP);
  or or_11 (ALUControl[0], SUB, SUBI, NOR, NORI, SRA);
  or or_12 (ALUControl[1], NAND, NANDI, NOR, NORI, LUI);
  or or_13 (ALUControl[2], SRL, SRA, LUI);
  and and_8 (PCSrc, or_7_out, T1_Execute);
  or or_14 (SPWrite, and_6_out, and_7_out);
  or or_15 (RegWrite, and_4_out, and_5_out, T3_Write_Back);
  or or_16 (or_16_out, LD, POP);
  Register #(.width(3)) State_register (.D(Next_State), .Q(Current_State), .clk(Clk), .clr(Reset));  // open: en
  Multiplexer #(.width(3), .enable("false")) multiplexer_1 (.in0(3'b000), .in1(3'b010), .out(State1), .sel(or_17_out));
  or or_17 (or_17_out, LD, ST, SPControl, POP);
  Multiplexer #(.width(3), .enable("false")) multiplexer_2 (.in0(3'b000), .in1(3'b011), .out(State2), .sel(or_16_out));
  Decoder #(.select(3), .enable("false")) decoder_2 (
    .out0(IRWrite), .out1(T1_Execute), .out2(T2_Mem_Access), .out3(T3_Write_Back), .sel(Current_State));  // open: out4, out5, out6, out7
  Multiplexer #(.select(3), .width(3), .enable("false")) multiplexer_3 (
    .in0(3'b001), .in1(State1), .in2(State2), .in3(3'b000), .in4(3'b000), .in5(3'b000), .in6(3'b000),
    .in7(3'b000), .out(Next_State), .sel(Current_State));

  assign RegSrc = MemToReg[1];

  // Other names for the same wires on the sheet: JAL = MemToReg[1]; PUSH = SPControl; T0_Fetch = IRWrite

  // Notes on the sheet:
  //   Yazma Yok
  //   Use_Imm
endmodule

module RegisterFile (
  input  [3:0] ReadReg1,
  input  [17:0] Write_Data,
  input  RegWrite,
  input  [3:0] WriteReg,
  input  [3:0] ReadReg2,
  input  Clk,
  output [17:0] ReadData1,
  output [17:0] ReadData2
);

  wire decoder_1_out0, decoder_1_out1, decoder_1_out2, decoder_1_out3, decoder_1_out4, decoder_1_out5,
       decoder_1_out6, decoder_1_out7, decoder_1_out8, decoder_1_out9, decoder_1_out10, decoder_1_out11,
       decoder_1_out12, decoder_1_out13, decoder_1_out14, decoder_1_out15;
  wire [17:0] R0_output, R1_output, R2_output, R3_output, R4_output, R5_output, R6_output, R7_output,
       R8_output, R9_output, R10_output, R11_output, R12_output, R13_output, R14_output, R15_output;

  Decoder #(.select(4), .disabled(0)) decoder_1 (
    .out0(decoder_1_out0), .out1(decoder_1_out1), .out2(decoder_1_out2), .out3(decoder_1_out3),
    .out4(decoder_1_out4), .out5(decoder_1_out5), .out6(decoder_1_out6), .out7(decoder_1_out7),
    .out8(decoder_1_out8), .out9(decoder_1_out9), .out10(decoder_1_out10), .out11(decoder_1_out11),
    .out12(decoder_1_out12), .out13(decoder_1_out13), .out14(decoder_1_out14), .out15(decoder_1_out15),
    .sel(WriteReg), .en(RegWrite));
  _18bit_register R0 (.Data(Write_Data), .Enable(decoder_1_out0), .Clk(Clk), .Output(R0_output));
  _18bit_register R1 (.Data(Write_Data), .Enable(decoder_1_out1), .Clk(Clk), .Output(R1_output));
  _18bit_register R2 (.Data(Write_Data), .Enable(decoder_1_out2), .Clk(Clk), .Output(R2_output));
  _18bit_register R3 (.Data(Write_Data), .Enable(decoder_1_out3), .Clk(Clk), .Output(R3_output));
  _18bit_register R4 (.Data(Write_Data), .Enable(decoder_1_out4), .Clk(Clk), .Output(R4_output));
  _18bit_register R5 (.Data(Write_Data), .Enable(decoder_1_out5), .Clk(Clk), .Output(R5_output));
  _18bit_register R6 (.Data(Write_Data), .Enable(decoder_1_out6), .Clk(Clk), .Output(R6_output));
  _18bit_register R7 (.Data(Write_Data), .Enable(decoder_1_out7), .Clk(Clk), .Output(R7_output));
  _18bit_register R8 (.Data(Write_Data), .Enable(decoder_1_out8), .Clk(Clk), .Output(R8_output));
  _18bit_register R9 (.Data(Write_Data), .Enable(decoder_1_out9), .Clk(Clk), .Output(R9_output));
  _18bit_register R10 (.Data(Write_Data), .Enable(decoder_1_out10), .Clk(Clk), .Output(R10_output));
  _18bit_register R11 (.Data(Write_Data), .Enable(decoder_1_out11), .Clk(Clk), .Output(R11_output));
  _18bit_register R12 (.Data(Write_Data), .Enable(decoder_1_out12), .Clk(Clk), .Output(R12_output));
  _18bit_register R13 (.Data(Write_Data), .Enable(decoder_1_out13), .Clk(Clk), .Output(R13_output));
  _18bit_register R14 (.Data(Write_Data), .Enable(decoder_1_out14), .Clk(Clk), .Output(R14_output));
  _18bit_register R15 (.Data(Write_Data), .Enable(decoder_1_out15), .Clk(Clk), .Output(R15_output));
  Multiplexer #(.select(4), .width(18), .enable("false")) multiplexer_1 (
    .in0(R0_output), .in1(R1_output), .in2(R2_output), .in3(R3_output), .in4(R4_output), .in5(R5_output),
    .in6(R6_output), .in7(R7_output), .in8(R8_output), .in9(R9_output), .in10(R10_output), .in11(R11_output),
    .in12(R12_output), .in13(R13_output), .in14(R14_output), .in15(R15_output), .out(ReadData1),
    .sel(ReadReg1));
  Multiplexer #(.select(4), .width(18), .enable("false")) multiplexer_2 (
    .in0(R0_output), .in1(R1_output), .in2(R2_output), .in3(R3_output), .in4(R4_output), .in5(R5_output),
    .in6(R6_output), .in7(R7_output), .in8(R8_output), .in9(R9_output), .in10(R10_output), .in11(R11_output),
    .in12(R12_output), .in13(R13_output), .in14(R14_output), .in15(R15_output), .out(ReadData2),
    .sel(ReadReg2));
endmodule

module ALU (
  input  [17:0] A,
  input  [17:0] B,
  input  [2:0] ALUOp,
  output Zero_Flag,
  output [17:0] Result
);

  wire [17:0] n18bitadder_1_out_4, n18bitsubtractor_1_out_4, nand_1_out, nor_1_out, shifter_1_q;

  _18bitadder u_18bitadder_1 (.A(A), .B(B), .out_4(n18bitadder_1_out_4));  // open: CO
  _18bitSubtractor u_18bitsubtractor_1 (.A(A), .B(B), .out_4(n18bitsubtractor_1_out_4));  // open: CO
  assign nand_1_out = ~(A & B);  // NAND_Gate nand_1, 18 bits wide
  assign nor_1_out = ~(A | B);  // NOR_Gate nor_1, 18 bits wide
  Shifter shifter_1 (.DATA_IN(A), .SELECTED(ALUOp[0]), .ShiftAmount(B[4:0]), .Q(shifter_1_q));
  Multiplexer #(.select(3), .width(18), .enable("false")) multiplexer_1 (
    .in0(n18bitadder_1_out_4), .in1(n18bitsubtractor_1_out_4), .in2(nand_1_out), .in3(nor_1_out),
    .in4(shifter_1_q), .in5(shifter_1_q), .out(Result), .sel(ALUOp));  // open: in6, in7
  Comparator comparator_1 (.INPUT_A({18{1'b0}}), .INPUT_B(Result), .EQUAL(Zero_Flag));
endmodule

module adder (
  input  A,
  input  B,
  input  CI,
  output Q,
  output CO
);

  wire and_1_out, and_2_out, xor_1_out;

  xor xor_1 (xor_1_out, A, B);
  xor xor_2 (Q, xor_1_out, CI);
  and and_1 (and_1_out, CI, xor_1_out);
  and and_2 (and_2_out, A, B);
  or or_1 (CO, and_1_out, and_2_out);
endmodule

module _18bitSubtractor (
  input  [17:0] A,
  input  [17:0] B,
  output CO,
  output [17:0] out_4
);

  wire adder_1_co, adder_2_co, adder_3_co, adder_4_co, adder_5_co, adder_6_co, adder_7_co, adder_8_co,
       adder_9_co, adder_10_co, adder_11_co, adder_12_co, adder_13_co, adder_14_co, adder_15_co, adder_16_co,
       adder_17_co;
  wire [17:0] not_1_out;

  assign not_1_out = ~B;  // NOT_Gate not_1, 18 bits wide
  adder adder_1 (.A(A[0]), .B(not_1_out[0]), .CI(1'b1), .Q(out_4[0]), .CO(adder_1_co));
  adder adder_2 (.A(A[1]), .B(not_1_out[1]), .CI(adder_1_co), .Q(out_4[1]), .CO(adder_2_co));
  adder adder_3 (.A(A[2]), .B(not_1_out[2]), .CI(adder_2_co), .Q(out_4[2]), .CO(adder_3_co));
  adder adder_4 (.A(A[3]), .B(not_1_out[3]), .CI(adder_3_co), .Q(out_4[3]), .CO(adder_4_co));
  adder adder_5 (.A(A[4]), .B(not_1_out[4]), .CI(adder_4_co), .Q(out_4[4]), .CO(adder_5_co));
  adder adder_6 (.A(A[5]), .B(not_1_out[5]), .CI(adder_5_co), .Q(out_4[5]), .CO(adder_6_co));
  adder adder_7 (.A(A[6]), .B(not_1_out[6]), .CI(adder_6_co), .Q(out_4[6]), .CO(adder_7_co));
  adder adder_8 (.A(A[7]), .B(not_1_out[7]), .CI(adder_7_co), .Q(out_4[7]), .CO(adder_8_co));
  adder adder_9 (.A(A[8]), .B(not_1_out[8]), .CI(adder_8_co), .Q(out_4[8]), .CO(adder_9_co));
  adder adder_10 (.A(A[9]), .B(not_1_out[9]), .CI(adder_9_co), .Q(out_4[9]), .CO(adder_10_co));
  adder adder_11 (.A(A[10]), .B(not_1_out[10]), .CI(adder_10_co), .Q(out_4[10]), .CO(adder_11_co));
  adder adder_12 (.A(A[11]), .B(not_1_out[11]), .CI(adder_11_co), .Q(out_4[11]), .CO(adder_12_co));
  adder adder_13 (.A(A[12]), .B(not_1_out[12]), .CI(adder_12_co), .Q(out_4[12]), .CO(adder_13_co));
  adder adder_14 (.A(A[13]), .B(not_1_out[13]), .CI(adder_13_co), .Q(out_4[13]), .CO(adder_14_co));
  adder adder_15 (.A(A[14]), .B(not_1_out[14]), .CI(adder_14_co), .Q(out_4[14]), .CO(adder_15_co));
  adder adder_16 (.A(A[15]), .B(not_1_out[15]), .CI(adder_15_co), .Q(out_4[15]), .CO(adder_16_co));
  adder adder_17 (.A(A[16]), .B(not_1_out[16]), .CI(adder_16_co), .Q(out_4[16]), .CO(adder_17_co));
  adder adder_18 (.A(A[17]), .B(not_1_out[17]), .CI(adder_17_co), .Q(out_4[17]), .CO(CO));
endmodule

module _18bitadder (
  input  [17:0] A,
  input  [17:0] B,
  output CO,
  output [17:0] out_4
);

  wire adder_1_co, adder_2_co, adder_3_co, adder_4_co, adder_5_co, adder_6_co, adder_7_co, adder_8_co,
       adder_9_co, adder_10_co, adder_11_co, adder_12_co, adder_13_co, adder_14_co, adder_15_co, adder_16_co,
       adder_17_co;

  adder adder_1 (.A(A[0]), .B(B[0]), .CI(1'b0), .Q(out_4[0]), .CO(adder_1_co));
  adder adder_2 (.A(A[1]), .B(B[1]), .CI(adder_1_co), .Q(out_4[1]), .CO(adder_2_co));
  adder adder_3 (.A(A[2]), .B(B[2]), .CI(adder_2_co), .Q(out_4[2]), .CO(adder_3_co));
  adder adder_4 (.A(A[3]), .B(B[3]), .CI(adder_3_co), .Q(out_4[3]), .CO(adder_4_co));
  adder adder_5 (.A(A[4]), .B(B[4]), .CI(adder_4_co), .Q(out_4[4]), .CO(adder_5_co));
  adder adder_6 (.A(A[5]), .B(B[5]), .CI(adder_5_co), .Q(out_4[5]), .CO(adder_6_co));
  adder adder_7 (.A(A[6]), .B(B[6]), .CI(adder_6_co), .Q(out_4[6]), .CO(adder_7_co));
  adder adder_8 (.A(A[7]), .B(B[7]), .CI(adder_7_co), .Q(out_4[7]), .CO(adder_8_co));
  adder adder_9 (.A(A[8]), .B(B[8]), .CI(adder_8_co), .Q(out_4[8]), .CO(adder_9_co));
  adder adder_10 (.A(A[9]), .B(B[9]), .CI(adder_9_co), .Q(out_4[9]), .CO(adder_10_co));
  adder adder_11 (.A(A[10]), .B(B[10]), .CI(adder_10_co), .Q(out_4[10]), .CO(adder_11_co));
  adder adder_12 (.A(A[11]), .B(B[11]), .CI(adder_11_co), .Q(out_4[11]), .CO(adder_12_co));
  adder adder_13 (.A(A[12]), .B(B[12]), .CI(adder_12_co), .Q(out_4[12]), .CO(adder_13_co));
  adder adder_14 (.A(A[13]), .B(B[13]), .CI(adder_13_co), .Q(out_4[13]), .CO(adder_14_co));
  adder adder_15 (.A(A[14]), .B(B[14]), .CI(adder_14_co), .Q(out_4[14]), .CO(adder_15_co));
  adder adder_16 (.A(A[15]), .B(B[15]), .CI(adder_15_co), .Q(out_4[15]), .CO(adder_16_co));
  adder adder_17 (.A(A[16]), .B(B[16]), .CI(adder_16_co), .Q(out_4[16]), .CO(adder_17_co));
  adder adder_18 (.A(A[17]), .B(B[17]), .CI(adder_17_co), .Q(out_4[17]), .CO(CO));
endmodule

module Shifter (
  input  [17:0] DATA_IN,
  input  SELECTED,
  input  [4:0] ShiftAmount,
  output [17:0] Q
);

  wire [17:0] multiplexer_2_out, multiplexer_3_out, multiplexer_4_out, multiplexer_5_out;
  wire [17:17] multiplexer_1_out;

  Multiplexer multiplexer_1 (.in0(1'b0), .in1(DATA_IN[17]), .out(multiplexer_1_out[17]), .sel(SELECTED));  // open: en
  Multiplexer #(.width(18)) multiplexer_2 (
    .in0(DATA_IN), .in1({multiplexer_1_out[17], DATA_IN[17:1]}), .out(multiplexer_2_out), .sel(ShiftAmount[0]));  // open: en
  Multiplexer #(.width(18)) multiplexer_3 (
    .in0(multiplexer_2_out), .in1({{2{multiplexer_1_out[17]}}, multiplexer_2_out[17:2]}),
    .out(multiplexer_3_out), .sel(ShiftAmount[1]));  // open: en
  Multiplexer #(.width(18)) multiplexer_4 (
    .in0(multiplexer_3_out), .in1({{4{multiplexer_1_out[17]}}, multiplexer_3_out[17:4]}),
    .out(multiplexer_4_out), .sel(ShiftAmount[2]));  // open: en
  Multiplexer #(.width(18)) multiplexer_5 (
    .in0(multiplexer_4_out), .in1({{8{multiplexer_1_out[17]}}, multiplexer_4_out[17:8]}),
    .out(multiplexer_5_out), .sel(ShiftAmount[3]));  // open: en
  Multiplexer #(.width(18)) multiplexer_6 (
    .in0(multiplexer_5_out), .in1({{16{multiplexer_1_out[17]}}, multiplexer_5_out[17:16]}), .out(Q),
    .sel(ShiftAmount[4]));  // open: en
endmodule

module Comparator (
  input  [17:0] INPUT_A,
  input  [17:0] INPUT_B,
  output EQUAL
);

  wire xnor_1_out, xnor_2_out, xnor_3_out, xnor_4_out, xnor_5_out, xnor_6_out, xnor_7_out, xnor_8_out,
       xnor_9_out, xnor_10_out, xnor_11_out, xnor_12_out, xnor_13_out, xnor_14_out, xnor_15_out, xnor_16_out,
       xnor_17_out, xnor_18_out;

  xnor xnor_1 (xnor_1_out, INPUT_A[0], INPUT_B[0]);
  xnor xnor_2 (xnor_2_out, INPUT_A[1], INPUT_B[1]);
  xnor xnor_3 (xnor_3_out, INPUT_A[2], INPUT_B[2]);
  xnor xnor_4 (xnor_4_out, INPUT_A[3], INPUT_B[3]);
  xnor xnor_5 (xnor_5_out, INPUT_A[4], INPUT_B[4]);
  xnor xnor_6 (xnor_6_out, INPUT_A[5], INPUT_B[5]);
  xnor xnor_7 (xnor_7_out, INPUT_A[6], INPUT_B[6]);
  xnor xnor_8 (xnor_8_out, INPUT_A[7], INPUT_B[7]);
  xnor xnor_9 (xnor_9_out, INPUT_A[8], INPUT_B[8]);
  xnor xnor_10 (xnor_10_out, INPUT_A[9], INPUT_B[9]);
  xnor xnor_11 (xnor_11_out, INPUT_A[10], INPUT_B[10]);
  xnor xnor_12 (xnor_12_out, INPUT_A[11], INPUT_B[11]);
  xnor xnor_13 (xnor_13_out, INPUT_A[12], INPUT_B[12]);
  xnor xnor_14 (xnor_14_out, INPUT_A[13], INPUT_B[13]);
  xnor xnor_15 (xnor_15_out, INPUT_A[14], INPUT_B[14]);
  xnor xnor_16 (xnor_16_out, INPUT_A[15], INPUT_B[15]);
  xnor xnor_17 (xnor_17_out, INPUT_A[16], INPUT_B[16]);
  xnor xnor_18 (xnor_18_out, INPUT_A[17], INPUT_B[17]);
  and and_1 (EQUAL, xnor_1_out, xnor_2_out, xnor_3_out, xnor_4_out, xnor_5_out, xnor_6_out, xnor_7_out, xnor_8_out, xnor_9_out, xnor_11_out, xnor_12_out, xnor_13_out, xnor_14_out, xnor_15_out, xnor_16_out, xnor_17_out, xnor_18_out);
endmodule

module _1bit_register (
  input  Data,
  input  Enable,
  input  Clk,
  output Output
);

  D_Flip_Flop d_ff_1 (.clk(Clk), .D(Data), .Q(Output), .en(Enable));  // open: Qn, preset, reset
endmodule

module _4bit_register (
  input  [3:0] Data,
  input  Enable,
  input  Clk,
  output [3:0] Output
);

  D_Flip_Flop d_ff_1 (.clk(Clk), .D(Data[0]), .Q(Output[0]), .en(Enable));  // open: Qn, preset, reset
  D_Flip_Flop d_ff_2 (.clk(Clk), .D(Data[1]), .Q(Output[1]), .en(Enable));  // open: Qn, preset, reset
  D_Flip_Flop d_ff_3 (.clk(Clk), .D(Data[2]), .Q(Output[2]), .en(Enable));  // open: Qn, preset, reset
  D_Flip_Flop d_ff_4 (.clk(Clk), .D(Data[3]), .Q(Output[3]), .en(Enable));  // open: Qn, preset, reset
endmodule

module _12bit_register (
  input  [11:0] Data,
  input  Enable,
  input  Clk,
  output [11:0] Output
);

  D_Flip_Flop d_ff_1 (.clk(Clk), .D(Data[0]), .Q(Output[0]), .en(Enable));  // open: Qn, preset, reset
  D_Flip_Flop d_ff_2 (.clk(Clk), .D(Data[1]), .Q(Output[1]), .en(Enable));  // open: Qn, preset, reset
  D_Flip_Flop d_ff_3 (.clk(Clk), .D(Data[2]), .Q(Output[2]), .en(Enable));  // open: Qn, preset, reset
  D_Flip_Flop d_ff_4 (.clk(Clk), .D(Data[3]), .Q(Output[3]), .en(Enable));  // open: Qn, preset, reset
  D_Flip_Flop d_ff_5 (.clk(Clk), .D(Data[4]), .Q(Output[4]), .en(Enable));  // open: Qn, preset, reset
  D_Flip_Flop d_ff_6 (.clk(Clk), .D(Data[5]), .Q(Output[5]), .en(Enable));  // open: Qn, preset, reset
  D_Flip_Flop d_ff_7 (.clk(Clk), .D(Data[6]), .Q(Output[6]), .en(Enable));  // open: Qn, preset, reset
  D_Flip_Flop d_ff_8 (.clk(Clk), .D(Data[7]), .Q(Output[7]), .en(Enable));  // open: Qn, preset, reset
  D_Flip_Flop d_ff_9 (.clk(Clk), .D(Data[8]), .Q(Output[8]), .en(Enable));  // open: Qn, preset, reset
  D_Flip_Flop d_ff_10 (.clk(Clk), .D(Data[9]), .Q(Output[9]), .en(Enable));  // open: Qn, preset, reset
  D_Flip_Flop d_ff_11 (.clk(Clk), .D(Data[10]), .Q(Output[10]), .en(Enable));  // open: Qn, preset, reset
  D_Flip_Flop d_ff_12 (.clk(Clk), .D(Data[11]), .Q(Output[11]), .en(Enable));  // open: Qn, preset, reset
endmodule

module _18bit_register (
  input  [17:0] Data,
  input  Enable,
  input  Clk,
  output [17:0] Output
);

  D_Flip_Flop d_ff_1 (.clk(Clk), .D(Data[0]), .Q(Output[0]), .en(Enable));  // open: Qn, preset, reset
  D_Flip_Flop d_ff_2 (.clk(Clk), .D(Data[1]), .Q(Output[1]), .en(Enable));  // open: Qn, preset, reset
  D_Flip_Flop d_ff_3 (.clk(Clk), .D(Data[2]), .Q(Output[2]), .en(Enable));  // open: Qn, preset, reset
  D_Flip_Flop d_ff_4 (.clk(Clk), .D(Data[3]), .Q(Output[3]), .en(Enable));  // open: Qn, preset, reset
  D_Flip_Flop d_ff_5 (.clk(Clk), .D(Data[4]), .Q(Output[4]), .en(Enable));  // open: Qn, preset, reset
  D_Flip_Flop d_ff_6 (.clk(Clk), .D(Data[5]), .Q(Output[5]), .en(Enable));  // open: Qn, preset, reset
  D_Flip_Flop d_ff_7 (.clk(Clk), .D(Data[6]), .Q(Output[6]), .en(Enable));  // open: Qn, preset, reset
  D_Flip_Flop d_ff_8 (.clk(Clk), .D(Data[7]), .Q(Output[7]), .en(Enable));  // open: Qn, preset, reset
  D_Flip_Flop d_ff_9 (.clk(Clk), .D(Data[8]), .Q(Output[8]), .en(Enable));  // open: Qn, preset, reset
  D_Flip_Flop d_ff_10 (.clk(Clk), .D(Data[9]), .Q(Output[9]), .en(Enable));  // open: Qn, preset, reset
  D_Flip_Flop d_ff_11 (.clk(Clk), .D(Data[10]), .Q(Output[10]), .en(Enable));  // open: Qn, preset, reset
  D_Flip_Flop d_ff_12 (.clk(Clk), .D(Data[11]), .Q(Output[11]), .en(Enable));  // open: Qn, preset, reset
  D_Flip_Flop d_ff_13 (.clk(Clk), .D(Data[12]), .Q(Output[12]), .en(Enable));  // open: Qn, preset, reset
  D_Flip_Flop d_ff_14 (.clk(Clk), .D(Data[13]), .Q(Output[13]), .en(Enable));  // open: Qn, preset, reset
  D_Flip_Flop d_ff_15 (.clk(Clk), .D(Data[14]), .Q(Output[14]), .en(Enable));  // open: Qn, preset, reset
  D_Flip_Flop d_ff_16 (.clk(Clk), .D(Data[15]), .Q(Output[15]), .en(Enable));  // open: Qn, preset, reset
  D_Flip_Flop d_ff_17 (.clk(Clk), .D(Data[16]), .Q(Output[16]), .en(Enable));  // open: Qn, preset, reset
  D_Flip_Flop d_ff_18 (.clk(Clk), .D(Data[17]), .Q(Output[17]), .en(Enable));  // open: Qn, preset, reset
endmodule

module _12bitADDER (
  input  [11:0] A,
  input  [11:0] B,
  output CO,
  output [11:0] Q
);

  wire adder_1_co, adder_2_co, adder_3_co, adder_4_co, adder_5_co, adder_6_co, adder_7_co, adder_8_co,
       adder_9_co, adder_10_co, adder_11_co;

  adder adder_1 (.A(A[0]), .B(B[0]), .CI(1'b0), .Q(Q[0]), .CO(adder_1_co));
  adder adder_2 (.A(A[1]), .B(B[1]), .CI(adder_1_co), .Q(Q[1]), .CO(adder_2_co));
  adder adder_3 (.A(A[2]), .B(B[2]), .CI(adder_2_co), .Q(Q[2]), .CO(adder_3_co));
  adder adder_4 (.A(A[3]), .B(B[3]), .CI(adder_3_co), .Q(Q[3]), .CO(adder_4_co));
  adder adder_5 (.A(A[4]), .B(B[4]), .CI(adder_4_co), .Q(Q[4]), .CO(adder_5_co));
  adder adder_6 (.A(A[5]), .B(B[5]), .CI(adder_5_co), .Q(Q[5]), .CO(adder_6_co));
  adder adder_7 (.A(A[6]), .B(B[6]), .CI(adder_6_co), .Q(Q[6]), .CO(adder_7_co));
  adder adder_8 (.A(A[7]), .B(B[7]), .CI(adder_7_co), .Q(Q[7]), .CO(adder_8_co));
  adder adder_9 (.A(A[8]), .B(B[8]), .CI(adder_8_co), .Q(Q[8]), .CO(adder_9_co));
  adder adder_10 (.A(A[9]), .B(B[9]), .CI(adder_9_co), .Q(Q[9]), .CO(adder_10_co));
  adder adder_11 (.A(A[10]), .B(B[10]), .CI(adder_10_co), .Q(Q[10]), .CO(adder_11_co));
  adder adder_12 (.A(A[11]), .B(B[11]), .CI(adder_11_co), .Q(Q[11]), .CO(CO));
endmodule

module _12bitSUBTRACTOR (
  input  [11:0] A,
  input  [11:0] B,
  output CO,
  output [11:0] CO_2
);

  wire adder_1_co, adder_2_co, adder_3_co, adder_4_co, adder_5_co, adder_6_co, adder_7_co, adder_8_co,
       adder_9_co, adder_10_co, adder_11_co;
  wire [11:0] not_1_out;

  assign not_1_out = ~B;  // NOT_Gate not_1, 12 bits wide
  adder adder_1 (.A(A[0]), .B(not_1_out[0]), .CI(1'b1), .Q(CO_2[0]), .CO(adder_1_co));
  adder adder_2 (.A(A[1]), .B(not_1_out[1]), .CI(adder_1_co), .Q(CO_2[1]), .CO(adder_2_co));
  adder adder_3 (.A(A[2]), .B(not_1_out[2]), .CI(adder_2_co), .Q(CO_2[2]), .CO(adder_3_co));
  adder adder_4 (.A(A[3]), .B(not_1_out[3]), .CI(adder_3_co), .Q(CO_2[3]), .CO(adder_4_co));
  adder adder_5 (.A(A[4]), .B(not_1_out[4]), .CI(adder_4_co), .Q(CO_2[4]), .CO(adder_5_co));
  adder adder_6 (.A(A[5]), .B(not_1_out[5]), .CI(adder_5_co), .Q(CO_2[5]), .CO(adder_6_co));
  adder adder_7 (.A(A[6]), .B(not_1_out[6]), .CI(adder_6_co), .Q(CO_2[6]), .CO(adder_7_co));
  adder adder_8 (.A(A[7]), .B(not_1_out[7]), .CI(adder_7_co), .Q(CO_2[7]), .CO(adder_8_co));
  adder adder_9 (.A(A[8]), .B(not_1_out[8]), .CI(adder_8_co), .Q(CO_2[8]), .CO(adder_9_co));
  adder adder_10 (.A(A[9]), .B(not_1_out[9]), .CI(adder_9_co), .Q(CO_2[9]), .CO(adder_10_co));
  adder adder_11 (.A(A[10]), .B(not_1_out[10]), .CI(adder_10_co), .Q(CO_2[10]), .CO(adder_11_co));
  adder adder_12 (.A(A[11]), .B(not_1_out[11]), .CI(adder_11_co), .Q(CO_2[11]), .CO(CO));
endmodule
